# Fritzing sketch Circuit (saved by Fritzing 0.9.3b)
breadboards: 1

parts:
  Part1 = Bluetooth HC-05 Macho
  Part2 = Arduino Uno (Rev3) - ICSP
  C2 = Capacitor Polarized [package=panasonic_e]  # not connected
  R2 = Resistor [tolerance=±5% resistance=220 package="1206 [SMD]"]
  U2 = Sharp Dust Sensor [part_number=GP2Y1010AU0F]
  KY-2 = Keyes Relay [package=THT]
  J2 = Generic male header - 3 pins [form="♂ (male)" package=THT]

nets:
  N1: Part1.TXD, Part2.D2
  N2: Part1.RXD, Part2.D3_PWM
  VCC: Part1.VCC, R2.Pin_1, U2.LED, U2.VCC, KY-2.power
  GND: Part1.GND, Part2.GND, U2.LED-GND, KY-2.ground
  N3: Part2.A5/SCL, U2.Vo
  N4: Part2.D11_PWM/MOSI, KY-2.signal
  N5: R2.Pin_0, U2.V-LED
  N6: KY-2.C, J2.pin1

notes:
  220uf

custom parts:
  Sharp Dust Sensor: Sharp GP2Y1010AU0F Dust Sensor
  Keyes Relay: The Keyes 5V relay module is suitable for SCM development, home appliance control. It uses a 5V~12V TIL control signal which can control DC / AC signal.
  Generic male header - 3 pins: Generic male header
